# Fritzing sketch schematic (saved by Fritzing 0.9.5d)
breadboards: 1

parts:
  Part4 = Arduino Pro Micro (Clone)
  R1 = Resistor [tolerance=±5% resistance=220 package="0603 [SMD]"]
  S1 = Round Pushbutton

nets:
  N1: Part4.GND, R1.Pin_0, S1.leg1
  N2: Part4.A0, S1.leg0
  N3: Part4.VCC, R1.Pin_1
